# Fritzing sketch weather (saved by Fritzing 0.9.3b)
breadboards: 1

parts:
  Part1 = Arduino Uno (Rev3)
  U1 = ESP8266 WiFi Module [part_number=ESP8266]
  DHT1 = DHT11 Humitidy and Temperature Sensor
  R1 = Resistor [tolerance=±5% resistance=220 package=THT]

nets:
  GND: Part1.RESET, Part1.GND, U1.GPIO_0, U1.GND
  3V3: Part1.3V3, U1.VCC, U1.CH_PD
  5V: Part1.5V, DHT1.VDD, R1.Pin_0
  VIN: Part1.VIN, DHT1.GND
  N1: U1.GPIO_2, DHT1.NULL
  N2: DHT1.DATA, R1.Pin_1

custom parts:
  ESP8266 WiFi Module: Generic WiFi Module based on the ESP8266 with onboard PCB antenna and UART communications
  DHT11 Humitidy and Temperature Sensor: DHT11 Humidity and Temperature Sensor
